// Logisim project calculator_logism.circ as structural Verilog: 14 circuits, main circuit calculator_body
module calculator_body (
  input  N_9,
  input  N_8,
  input  N_7,
  input  N_6,
  input  N_5,
  input  N_4,
  input  N_3,
  input  N_2,
  input  N_1,
  input  N_0,
  input  ADD,
  input  SUB,
  input  MUL,
  input  DIV,
  input  equal,
  input  clear,
  output [3:0] D_7,
  output [3:0] D_6,
  output [3:0] D_5,
  output [3:0] D_4,
  output [3:0] D_3,
  output [3:0] D_2,
  output [3:0] D_1,
  output [3:0] D_0
);

  wire or_9_out, or_10_out;
  wire [1:0] alu_op_command_1_op_output;
  wire [3:0] digit_binary_output_1_d0, digit_binary_output_1_d1, digit_binary_output_1_d2,
       digit_binary_output_1_d3, digit_binary_output_1_d4, digit_binary_output_1_d5,
       digit_binary_output_1_d6, digit_binary_output_1_d7, double_dable_bcd_to_binary_1_digit_0,
       double_dable_bcd_to_binary_1_digit_1, double_dable_bcd_to_binary_1_digit_2,
       double_dable_bcd_to_binary_1_digit_3, double_dable_bcd_to_binary_1_digit_4,
       double_dable_bcd_to_binary_1_digit_5, double_dable_bcd_to_binary_1_digit_6,
       double_dable_bcd_to_binary_1_digit_7;
  wire [31:0] a_register_1_a_out, alu_1_result, b_register_1_b_out, digit_binary_output_1_binary_out,
       result_register_1_result_out;

  assign D_7 = double_dable_bcd_to_binary_1_digit_7 | digit_binary_output_1_d7;  // OR_Gate or_1, 4 bits wide
  assign D_6 = double_dable_bcd_to_binary_1_digit_6 | digit_binary_output_1_d6;  // OR_Gate or_2, 4 bits wide
  DOUBLE_DABLE_BCD_TO_BINARY double_dable_bcd_to_binary_1 (
    .BINARY_IN(result_register_1_result_out), .DIGIT_7(double_dable_bcd_to_binary_1_digit_7),
    .DIGIT_6(double_dable_bcd_to_binary_1_digit_6), .DIGIT_5(double_dable_bcd_to_binary_1_digit_5),
    .DIGIT_4(double_dable_bcd_to_binary_1_digit_4), .DIGIT_3(double_dable_bcd_to_binary_1_digit_3),
    .DIGIT_2(double_dable_bcd_to_binary_1_digit_2), .DIGIT_1(double_dable_bcd_to_binary_1_digit_1),
    .DIGIT_0(double_dable_bcd_to_binary_1_digit_0));
  assign D_5 = double_dable_bcd_to_binary_1_digit_5 | digit_binary_output_1_d5;  // OR_Gate or_3, 4 bits wide
  assign D_4 = double_dable_bcd_to_binary_1_digit_4 | digit_binary_output_1_d4;  // OR_Gate or_4, 4 bits wide
  assign D_3 = double_dable_bcd_to_binary_1_digit_3 | digit_binary_output_1_d3;  // OR_Gate or_5, 4 bits wide
  DIGIT_BINARY_OUtput digit_binary_output_1 (
    .n0(N_0), .n1(N_1), .n2(N_2), .n3(N_3), .n4(N_4), .n5(N_5), .n6(N_6), .n7(N_7), .n8(N_8), .n9(N_9),
    .clear(or_9_out), .D7(digit_binary_output_1_d7), .D6(digit_binary_output_1_d6),
    .D5(digit_binary_output_1_d5), .D4(digit_binary_output_1_d4), .D3(digit_binary_output_1_d3),
    .D2(digit_binary_output_1_d2), .D1(digit_binary_output_1_d1), .D0(digit_binary_output_1_d0),
    .Binary_Out(digit_binary_output_1_binary_out));
  assign D_2 = double_dable_bcd_to_binary_1_digit_2 | digit_binary_output_1_d2;  // OR_Gate or_6, 4 bits wide
  assign D_1 = double_dable_bcd_to_binary_1_digit_1 | digit_binary_output_1_d1;  // OR_Gate or_7, 4 bits wide
  assign D_0 = double_dable_bcd_to_binary_1_digit_0 | digit_binary_output_1_d0;  // OR_Gate or_8, 4 bits wide
  or or_9 (or_9_out, clear, equal, or_10_out);
  or or_10 (or_10_out, ADD, SUB, MUL, DIV);
  Hex_Digit_Display hex_digit_display_1 ();  // open: value, dp
  Hex_Digit_Display hex_digit_display_2 ();  // open: value, dp
  Hex_Digit_Display hex_digit_display_3 ();  // open: value, dp
  Hex_Digit_Display hex_digit_display_4 ();  // open: value, dp
  Hex_Digit_Display hex_digit_display_5 ();  // open: value, dp
  A_register a_register_1 (
    .DATA_IN(digit_binary_output_1_binary_out), .LOAD_A(or_10_out), .CLEAR_A(clear),
    .A_OUT(a_register_1_a_out));
  B_register b_register_1 (
    .DATA_IN(digit_binary_output_1_binary_out), .LOAD_B(equal), .CLEAR_B(clear), .B_OUT(b_register_1_b_out));
  Hex_Digit_Display hex_digit_display_6 ();  // open: value, dp
  Hex_Digit_Display hex_digit_display_7 ();  // open: value, dp
  ALU_OP_COMMAND alu_op_command_1 (
    .ADD(ADD), .SUB(SUB), .MUL(MUL), .DIV(DIV), .CLEAR(clear), .OP_OUTPUT(alu_op_command_1_op_output));
  Hex_Digit_Display hex_digit_display_8 ();  // open: value, dp
  ALU alu_1 (
    .A_input(a_register_1_a_out), .B_input(b_register_1_b_out), .ALU_OP(alu_op_command_1_op_output),
    .RESULT(alu_1_result));  // open: OVERFLOW, CARRY
  RESULT_REGISTER result_register_1 (
    .DATA_IN(alu_1_result), .LOAD_RESULT(equal), .CLEAR_RESULT(clear),
    .RESULT_OUT(result_register_1_result_out));
endmodule

module digit_input (
  input  n0,
  input  n1,
  input  n2,
  input  n3,
  input  n4,
  input  n5,
  input  n6,
  input  n7,
  input  n8,
  input  n9,
  input  clear,
  output [3:0] D7,
  output [3:0] D6,
  output [3:0] D5,
  output [3:0] D4,
  output [3:0] D3,
  output [3:0] D2,
  output [3:0] D1,
  output [3:0] D0
);

  wire not_1_out, priority_encoder_1_en_out;
  wire [3:0] priority_encoder_1_out;

  Priority_Encoder #(.select(4)) priority_encoder_1 (
    .in0(n0), .in1(n1), .in2(n2), .in3(n3), .in4(n4), .in5(n5), .in6(n6), .in7(n7), .in8(n8), .in9(n9),
    .out(priority_encoder_1_out), .en_out(priority_encoder_1_en_out));  // open: in10, in11, in12, in13, in14, in15, gs, en_in
  not not_1 (not_1_out, priority_encoder_1_en_out);
  Register #(.width(4)) register_1 (.D(D6), .clk(not_1_out), .Q(D7), .clr(clear));  // open: en
  Hex_Digit_Display hex_digit_display_1 ();  // open: value, dp
  Hex_Digit_Display hex_digit_display_2 ();  // open: value, dp
  Hex_Digit_Display hex_digit_display_3 ();  // open: value, dp
  Register #(.width(4)) register_2 (.D(D5), .clk(not_1_out), .Q(D6), .clr(clear));  // open: en
  Hex_Digit_Display hex_digit_display_4 ();  // open: value, dp
  Hex_Digit_Display hex_digit_display_5 ();  // open: value, dp
  Register #(.width(4)) register_3 (.D(D4), .clk(not_1_out), .Q(D5), .clr(clear));  // open: en
  Hex_Digit_Display hex_digit_display_6 ();  // open: value, dp
  Hex_Digit_Display hex_digit_display_7 ();  // open: value, dp
  Hex_Digit_Display hex_digit_display_8 ();  // open: value, dp
  Register #(.width(4)) register_4 (.D(D3), .clk(not_1_out), .Q(D4), .clr(clear));  // open: en
  Register #(.width(4)) register_5 (.D(D2), .clk(not_1_out), .Q(D3), .clr(clear));  // open: en
  Register #(.width(4)) register_6 (.D(D1), .clk(not_1_out), .Q(D2), .clr(clear));  // open: en
  Register #(.width(4)) register_7 (.D(D0), .clk(not_1_out), .Q(D1), .clr(clear));  // open: en
  Register #(.width(4)) register_8 (.D(priority_encoder_1_out), .clk(not_1_out), .Q(D0), .clr(clear));  // open: en
endmodule

module A_register (
  input  [31:0] DATA_IN,
  input  LOAD_A,
  input  CLEAR_A,
  output [31:0] A_OUT
);

  Register #(.width(32)) register_1 (.D(DATA_IN), .clk(LOAD_A), .Q(A_OUT), .clr(CLEAR_A));  // open: en
endmodule

module B_register (
  input  [31:0] DATA_IN,
  input  LOAD_B,
  input  CLEAR_B,
  output [31:0] B_OUT
);

  Register #(.width(32)) register_1 (.D(DATA_IN), .clk(LOAD_B), .Q(B_OUT), .clr(CLEAR_B));  // open: en
endmodule

module BCD_to_Binary (
  input  [3:0] D7,
  input  [3:0] D6,
  input  [3:0] D5,
  input  [3:0] D4,
  input  [3:0] D3,
  input  [3:0] D2,
  input  [3:0] D1,
  input  [3:0] D0,
  output [31:0] BINARY_OUT_PUT
);

  wire [31:0] adder_1_out, adder_2_out, adder_3_out, adder_4_out, adder_5_out, adder_6_out,
       bit_extender_1_out, bit_extender_2_out, bit_extender_3_out, bit_extender_4_out, bit_extender_5_out,
       bit_extender_6_out, bit_extender_7_out, bit_extender_8_out, multiplier_1_out, multiplier_2_out,
       multiplier_3_out, multiplier_4_out, multiplier_5_out, multiplier_6_out, multiplier_7_out;

  assign bit_extender_1_out = {{28{1'b0}}, D7};  // Bit_Extender bit_extender_1
  assign bit_extender_2_out = {{28{1'b0}}, D6};  // Bit_Extender bit_extender_2
  assign bit_extender_3_out = {{28{1'b0}}, D5};  // Bit_Extender bit_extender_3
  assign bit_extender_4_out = {{28{1'b0}}, D4};  // Bit_Extender bit_extender_4
  assign bit_extender_5_out = {{28{1'b0}}, D3};  // Bit_Extender bit_extender_5
  assign bit_extender_6_out = {{28{1'b0}}, D2};  // Bit_Extender bit_extender_6
  assign bit_extender_7_out = {{28{1'b0}}, D1};  // Bit_Extender bit_extender_7
  assign bit_extender_8_out = {{28{1'b0}}, D0};  // Bit_Extender bit_extender_8
  Multiplier #(.width(32)) multiplier_1 (.a(bit_extender_1_out), .b(32'ha), .out(multiplier_1_out));  // open: cin, cout
  Adder #(.width(32)) adder_1 (
    .a(multiplier_1_out), .b(bit_extender_2_out), .out(adder_1_out), .cin(1'b0));  // open: cout
  Multiplier #(.width(32)) multiplier_2 (.a(adder_1_out), .b(32'ha), .out(multiplier_2_out));  // open: cin, cout
  Adder #(.width(32)) adder_2 (
    .a(multiplier_2_out), .b(bit_extender_3_out), .out(adder_2_out), .cin(1'b0));  // open: cout
  Multiplier #(.width(32)) multiplier_3 (.a(adder_2_out), .b(32'ha), .out(multiplier_3_out));  // open: cin, cout
  Adder #(.width(32)) adder_3 (
    .a(multiplier_3_out), .b(bit_extender_4_out), .out(adder_3_out), .cin(1'b0));  // open: cout
  Multiplier #(.width(32)) multiplier_4 (.a(adder_3_out), .b(32'ha), .out(multiplier_4_out));  // open: cin, cout
  Adder #(.width(32)) adder_4 (
    .a(multiplier_4_out), .b(bit_extender_5_out), .out(adder_4_out), .cin(1'b0));  // open: cout
  Multiplier #(.width(32)) multiplier_5 (.a(adder_4_out), .b(32'ha), .out(multiplier_5_out));  // open: cin, cout
  Adder #(.width(32)) adder_5 (
    .a(multiplier_5_out), .b(bit_extender_6_out), .out(adder_5_out), .cin(1'b0));  // open: cout
  Multiplier #(.width(32)) multiplier_6 (.a(adder_5_out), .b(32'ha), .out(multiplier_6_out));  // open: cin, cout
  Adder #(.width(32)) adder_6 (
    .a(multiplier_6_out), .b(bit_extender_7_out), .out(adder_6_out), .cin(1'b0));  // open: cout
  Multiplier #(.width(32)) multiplier_7 (.a(adder_6_out), .b(32'ha), .out(multiplier_7_out));  // open: cin, cout
  Adder #(.width(32)) adder_7 (
    .a(multiplier_7_out), .b(bit_extender_8_out), .out(BINARY_OUT_PUT), .cin(1'b0));  // open: cout
  Hex_Digit_Display hex_digit_display_1 (.value(BINARY_OUT_PUT[3:0]));  // open: dp
endmodule

module ALU (
  input  [31:0] A_input,
  input  [31:0] B_input,
  input  [1:0] ALU_OP,
  output OVERFLOW,
  output [31:0] RESULT,
  output CARRY
);

  wire adder_1_cout, and_2_out, and_3_out, and_4_out, and_5_out, not_1_out, not_2_out, not_3_out, not_4_out,
       not_5_out, not_6_out, or_2_out, or_3_out, subtractor_1_bout;
  wire [31:0] adder_1_out, and_1_out, divider_1_out, multiplier_1_out, subtractor_1_out;

  Adder #(.width(32)) adder_1 (.a(A_input), .b(B_input), .out(adder_1_out), .cin(1'b0), .cout(adder_1_cout));
  Subtractor #(.width(32)) subtractor_1 (
    .a(A_input), .b(B_input), .out(subtractor_1_out), .bin(1'b0), .bout(subtractor_1_bout));
  Multiplier #(.width(32)) multiplier_1 (.a(A_input), .b(B_input), .out(multiplier_1_out));  // open: cin, cout
  Divider #(.width(32)) divider_1 (.a(A_input), .b(B_input), .out(divider_1_out));  // open: upper, rem
  // OR_Gate or_1 has open pins: in0=A_input, in1=B_input, out=open
  assign and_1_out = A_input & B_input;  // AND_Gate and_1, 32 bits wide
  not not_1 (not_1_out, A_input[31]);
  not not_2 (not_2_out, B_input[31]);
  not not_3 (not_3_out, adder_1_out[31]);
  Multiplexer #(.select(2), .width(32)) multiplexer_1 (
    .in0(adder_1_out), .in1(subtractor_1_out), .in2(multiplier_1_out), .in3(divider_1_out), .out(RESULT),
    .sel(ALU_OP));
  and and_2 (and_2_out, not_1_out, not_2_out, adder_1_out[31]);
  and and_3 (and_3_out, B_input[31], B_input[31], not_3_out);
  not not_4 (not_4_out, subtractor_1_out[31]);
  not not_5 (not_5_out, B_input[31]);
  not not_6 (not_6_out, A_input[31]);
  Multiplexer #(.select(2)) multiplexer_2 (
    .in0(adder_1_cout), .in1(subtractor_1_bout), .in2(1'b0), .in3(1'b0), .out(CARRY), .sel(ALU_OP));
  or or_2 (or_2_out, and_2_out, and_3_out);
  and and_4 (and_4_out, not_4_out, not_5_out, A_input[31]);
  and and_5 (and_5_out, subtractor_1_out[31], B_input[31], not_6_out);
  or or_3 (or_3_out, and_4_out, and_5_out);
  Multiplexer #(.select(2)) multiplexer_3 (
    .in0(or_2_out), .in1(or_3_out), .in2(1'b0), .in3(1'b0), .out(OVERFLOW), .sel(ALU_OP));
endmodule

module RESULT_REGISTER (
  input  [31:0] DATA_IN,
  input  LOAD_RESULT,
  input  CLEAR_RESULT,
  output [31:0] RESULT_OUT
);

  Register #(.width(32)) register_1 (.D(DATA_IN), .clk(LOAD_RESULT), .Q(RESULT_OUT), .clr(CLEAR_RESULT));  // open: en
endmodule

module DIGIT_BINARY_OUtput (
  input  n0,
  input  n1,
  input  n2,
  input  n3,
  input  n4,
  input  n5,
  input  n6,
  input  n7,
  input  n8,
  input  n9,
  input  clear,
  output [3:0] D7,
  output [3:0] D6,
  output [3:0] D5,
  output [3:0] D4,
  output [3:0] D3,
  output [3:0] D2,
  output [3:0] D1,
  output [3:0] D0,
  output [31:0] Binary_Out
);

  digit_input digit_input_1 (
    .n0(n0), .n1(n1), .n2(n2), .n3(n3), .n4(n4), .n5(n5), .n6(n6), .n7(n7), .n8(n8), .n9(n9), .clear(clear),
    .D7(D7), .D6(D6), .D5(D5), .D4(D4), .D3(D3), .D2(D2), .D1(D1), .D0(D0));
  BCD_to_Binary bcd_to_binary_1 (
    .D7(D7), .D6(D6), .D5(D5), .D4(D4), .D3(D3), .D2(D2), .D1(D1), .D0(D0), .BINARY_OUT_PUT(Binary_Out));
endmodule

module opporation_register (
  input  [1:0] OP_INPUT,
  input  OP_LOAD,
  input  OP_CLEAR,
  output [1:0] OP_RESULT
);

  Register #(.width(2)) register_1 (.D(OP_INPUT), .clk(OP_LOAD), .Q(OP_RESULT), .clr(OP_CLEAR));  // open: en
endmodule

module control_unit (
  input  DIGIT_ENTERED,
  input  OP_PRESSED,
  input  DIGIT_ENTERED_B,
  input  [2:0] NEXT_STATE,
  input  EQUAAL_PRESSED,
  input  CLOCK,
  input  RESET,
  output [2:0] IDEAL_NEXT,
  output [2:0] ENTER_A_NEXT,
  output [2:0] WAIT_OP_NEXT,
  output [2:0] ENTER_B_NEXT,
  output [2:0] CURRENT_STATE,
  output ENTER_A_STATE
);

  wire and_2_out, not_1_out, not_2_out;

  Multiplexer #(.width(3)) multiplexer_1 (.in0(3'b000), .in1(3'b001), .out(IDEAL_NEXT), .sel(DIGIT_ENTERED));
  Multiplexer #(.width(3)) multiplexer_2 (.in0(3'b001), .in1(3'b010), .out(ENTER_A_NEXT), .sel(OP_PRESSED));
  Multiplexer #(.width(3)) multiplexer_3 (.in0(3'b010), .in1(3'b011), .out(WAIT_OP_NEXT), .sel(DIGIT_ENTERED_B));
  Multiplexer #(.width(3)) multiplexer_4 (.in0(3'b011), .in1(3'b100), .out(ENTER_B_NEXT), .sel(EQUAAL_PRESSED));
  Multiplexer #(.select(3), .width(3)) multiplexer_5 (
    .in0(IDEAL_NEXT), .in1(ENTER_A_NEXT), .in2(WAIT_OP_NEXT), .in3(ENTER_B_NEXT), .in4(3'b101), .in5(3'b000),
    .in6(3'b000), .in7(3'b000), .out(NEXT_STATE), .sel(CURRENT_STATE));
  Register #(.width(3)) register_1 (.D(NEXT_STATE), .clk(CLOCK), .Q(CURRENT_STATE), .clr(RESET));  // open: en
  not not_1 (not_1_out, CURRENT_STATE[1]);
  not not_2 (not_2_out, CURRENT_STATE[2]);
  and and_1 (ENTER_A_STATE, CURRENT_STATE[0], not_1_out, not_2_out);
  and and_2 (and_2_out, ENTER_A_STATE, DIGIT_ENTERED_B);
endmodule

module ALU_OP_COMMAND (
  input  ADD,
  input  SUB,
  input  MUL,
  input  DIV,
  input  CLEAR,
  output [1:0] OP_OUTPUT
);

  wire or_1_out;
  wire [1:0] priority_encoder_1_out;

  Priority_Encoder #(.select(2)) priority_encoder_1 (
    .in0(ADD), .in1(SUB), .in2(MUL), .in3(DIV), .out(priority_encoder_1_out));  // open: gs, en_out, en_in
  or or_1 (or_1_out, ADD, SUB, MUL, DIV);
  Register #(.trigger("falling"), .width(2)) register_1 (
    .D(priority_encoder_1_out), .en(1'b1), .clk(or_1_out), .Q(OP_OUTPUT), .clr(CLEAR));
endmodule

module DABLE (
  input  B_3,
  input  B_2,
  input  B_1,
  input  B_0,
  output O_3,
  output O_2,
  output O_1,
  output O_0
);

  wire nor_1_out, nor_2_out, or_1_out, xor_1_out, xor_2_out;

  xor xor_1 (xor_1_out, B_0, B_3);
  nor nor_1 (nor_1_out, B_3, B_2);
  xor xor_2 (xor_2_out, B_3, B_1);
  nor nor_2 (nor_2_out, xor_1_out, xor_2_out);
  nor nor_3 (O_3, nor_2_out, nor_1_out);
  or or_1 (or_1_out, nor_1_out, xor_1_out);
  nor nor_4 (O_2, or_1_out, B_1);
  and and_1 (O_1, or_1_out, xor_2_out);
  xor xor_3 (O_0, O_3, B_0);
endmodule

module DOUBLE_DABLE_BCD_TO_BINARY (
  input  [31:0] BINARY_IN,
  output [3:0] DIGIT_7,
  output [3:0] DIGIT_6,
  output [3:0] DIGIT_5,
  output [3:0] DIGIT_4,
  output [3:0] DIGIT_3,
  output [3:0] DIGIT_2,
  output [3:0] DIGIT_1,
  output [3:0] DIGIT_0
);

  wire c3_0, c3_1, c3_2, c3_3, c4_0, c4_1, c4_2, c4_3, c5_0, c5_1, c5_2, c5_3, c6_0, c6_1, c6_2, c6_3, c6_4,
       c6_5, c6_6, c6_7, c7_0, c7_1, c7_2, c7_3, c7_4, c7_5, c7_6, c7_7, c8_0, c8_1, c8_2, c8_3, c8_4, c8_5,
       c8_6, c8_7, c9_0, c9_1, c9_2, c9_3, c9_4, c9_5, c9_6, c9_7, c9_8, c9_9, c9_10, c9_11, c10_0, c10_1,
       c10_2, c10_3, c10_4, c10_5, c10_6, c10_7, c10_8, c10_9, c10_10, c10_11, c11_0, c11_1, c11_2, c11_3,
       c11_4, c11_5, c11_6, c11_7, c11_8, c11_9, c11_10, c11_11, c12_0, c12_1, c12_2, c12_3, c12_4, c12_5,
       c12_6, c12_7, c12_8, c12_9, c12_10, c12_11, c13_0, c13_1, c13_2, c13_3, c13_4, c13_5, c13_6, c13_7,
       c13_8, c13_9, c13_10, c13_11, c13_12, c13_13, c13_14, c13_15, c14_0, c14_1, c14_2, c14_3, c14_4,
       c14_5, c14_6, c14_7, c14_8, c14_9, c14_10, c14_11, c14_12, c14_13, c14_14, c14_15, c15_0, c15_1,
       c15_2, c15_3, c15_4, c15_5, c15_6, c15_7, c15_8, c15_9, c15_10, c15_11, c15_12, c15_13, c15_14,
       c15_15, c16_0, c16_1, c16_2, c16_3, c16_4, c16_5, c16_6, c16_7, c16_8, c16_9, c16_10, c16_11, c16_12,
       c16_13, c16_14, c16_15, c16_16, c16_17, c16_18, c16_19, c17_0, c17_1, c17_2, c17_3, c17_4, c17_5,
       c17_6, c17_7, c17_8, c17_9, c17_10, c17_11, c17_12, c17_13, c17_14, c17_15, c17_16, c17_17, c17_18,
       c17_19, c18_0, c18_1, c18_2, c18_3, c18_4, c18_5, c18_6, c18_7, c18_8, c18_9, c18_10, c18_11, c18_12,
       c18_13, c18_14, c18_15, c18_16, c18_17, c18_18, c18_19, c19_0, c19_1, c19_2, c19_3, c19_4, c19_5,
       c19_6, c19_7, c19_8, c19_9, c19_10, c19_11, c19_12, c19_13, c19_14, c19_15, c19_16, c19_17, c19_18,
       c19_19, c19_20, c19_21, c19_22, c19_23, c20_0, c20_1, c20_2, c20_3, c20_4, c20_5, c20_6, c20_7, c20_8,
       c20_9, c20_10, c20_11, c20_12, c20_13, c20_14, c20_15, c20_16, c20_17, c20_18, c20_19, c20_20, c20_21,
       c20_22, c20_23, c21_0, c21_1, c21_2, c21_3, c21_4, c21_5, c21_6, c21_7, c21_8, c21_9, c21_10, c21_11,
       c21_12, c21_13, c21_14, c21_15, c21_16, c21_17, c21_18, c21_19, c21_20, c21_21, c21_22, c21_23, c22_0,
       c22_1, c22_2, c22_3, c22_4, c22_5, c22_6, c22_7, c22_8, c22_9, c22_10, c22_11, c22_12, c22_13, c22_14,
       c22_15, c22_16, c22_17, c22_18, c22_19, c22_20, c22_21, c22_22, c22_23, c23_0, c23_1, c23_2, c23_3,
       c23_4, c23_5, c23_6, c23_7, c23_8, c23_9, c23_10, c23_11, c23_12, c23_13, c23_14, c23_15, c23_16,
       c23_17, c23_18, c23_19, c23_20, c23_21, c23_22, c23_23, c23_24, c23_25, c23_26, c23_27, c24_0, c24_1,
       c24_2, c24_3, c24_4, c24_5, c24_6, c24_7, c24_8, c24_9, c24_10, c24_11, c24_12, c24_13, c24_14,
       c24_15, c24_16, c24_17, c24_18, c24_19, c24_20, c24_21, c24_22, c24_23, c24_24, c24_25, c24_26,
       c24_27, c25_0, c25_1, c25_2, c25_3, c25_4, c25_5, c25_6, c25_7, c25_8, c25_9, c25_10, c25_11, c25_12,
       c25_13, c25_14, c25_15, c25_16, c25_17, c25_18, c25_19, c25_20, c25_21, c25_22, c25_23, c25_24,
       c25_25, c25_26, c25_27, c26_0, c26_1, c26_2, c26_3, c26_4, c26_5, c26_6, c26_7, c26_8, c26_9, c26_10,
       c26_11, c26_12, c26_13, c26_14, c26_15, c26_16, c26_17, c26_18, c26_19, c26_20, c26_21, c26_22,
       c26_23, c26_24, c26_25, c26_26, c26_27, c26_28, c26_29, c26_30, c27_0, c27_1, c27_2, c27_3, c27_4,
       c27_5, c27_6, c27_7, c27_8, c27_9, c27_10, c27_11, c27_12, c27_13, c27_14, c27_15, c27_16, c27_17,
       c27_18, c27_19, c27_20, c27_21, c27_22, c27_23, c27_24, c27_25, c27_26, c27_27, c27_28, c27_29,
       c27_30, c28_0, c28_1, c28_2, c28_3, c28_4, c28_5, c28_6, c28_7, c28_8, c28_9, c28_10, c28_11, c28_12,
       c28_13, c28_14, c28_15, c28_16, c28_17, c28_18, c28_19, c28_20, c28_21, c28_22, c28_23, c28_24,
       c28_25, c28_26, c28_27, c28_28, c28_29, c28_30, c29_0, c29_1, c29_2, c29_3, c29_4, c29_5, c29_6,
       c29_7, c29_8, c29_9, c29_10, c29_11, c29_12, c29_13, c29_14, c29_15, c29_16, c29_17, c29_18, c29_19,
       c29_20, c29_21, c29_22, c29_23, c29_24, c29_25, c29_26, c29_27, c29_28, c29_29, c29_30, c30_0, c30_1,
       c30_2, c30_3, c30_4, c30_5, c30_6, c30_7, c30_8, c30_9, c30_10, c30_11, c30_12, c30_13, c30_14,
       c30_15, c30_16, c30_17, c30_18, c30_19, c30_20, c30_21, c30_22, c30_23, c30_24, c30_25, c30_26,
       c30_27, c30_28, c30_29, c30_30;

  DABLE dable_1 (
    .B_3(1'b0), .B_2(BINARY_IN[31]), .B_1(BINARY_IN[30]), .B_0(BINARY_IN[29]), .O_3(c3_3), .O_2(c3_2),
    .O_1(c3_1), .O_0(c3_0));
  DABLE dable_2 (
    .B_3(c3_2), .B_2(c3_1), .B_1(c3_0), .B_0(BINARY_IN[28]), .O_3(c4_3), .O_2(c4_2), .O_1(c4_1), .O_0(c4_0));
  DABLE dable_3 (
    .B_3(c4_2), .B_2(c4_1), .B_1(c4_0), .B_0(BINARY_IN[27]), .O_3(c5_3), .O_2(c5_2), .O_1(c5_1), .O_0(c5_0));
  DABLE dable_4 (
    .B_3(c5_2), .B_2(c5_1), .B_1(c5_0), .B_0(BINARY_IN[26]), .O_3(c6_3), .O_2(c6_2), .O_1(c6_1), .O_0(c6_0));
  DABLE dable_5 (.B_3(1'b0), .B_2(c3_3), .B_1(c4_3), .B_0(c5_3), .O_3(c6_7), .O_2(c6_6), .O_1(c6_5), .O_0(c6_4));
  DABLE dable_6 (
    .B_3(c6_2), .B_2(c6_1), .B_1(c6_0), .B_0(BINARY_IN[25]), .O_3(c7_3), .O_2(c7_2), .O_1(c7_1), .O_0(c7_0));
  DABLE dable_7 (.B_3(c6_6), .B_2(c6_5), .B_1(c6_4), .B_0(c6_3), .O_3(c7_7), .O_2(c7_6), .O_1(c7_5), .O_0(c7_4));
  DABLE dable_8 (
    .B_3(c7_2), .B_2(c7_1), .B_1(c7_0), .B_0(BINARY_IN[24]), .O_3(c8_3), .O_2(c8_2), .O_1(c8_1), .O_0(c8_0));
  DABLE dable_9 (.B_3(c7_6), .B_2(c7_5), .B_1(c7_4), .B_0(c7_3), .O_3(c8_7), .O_2(c8_6), .O_1(c8_5), .O_0(c8_4));
  DABLE dable_10 (
    .B_3(c8_2), .B_2(c8_1), .B_1(c8_0), .B_0(BINARY_IN[23]), .O_3(c9_3), .O_2(c9_2), .O_1(c9_1), .O_0(c9_0));
  DABLE dable_11 (.B_3(c8_6), .B_2(c8_5), .B_1(c8_4), .B_0(c8_3), .O_3(c9_7), .O_2(c9_6), .O_1(c9_5), .O_0(c9_4));
  DABLE dable_12 (.B_3(1'b0), .B_2(c6_7), .B_1(c7_7), .B_0(c8_7), .O_3(c9_11), .O_2(c9_10), .O_1(c9_9), .O_0(c9_8));
  DABLE dable_13 (
    .B_3(c9_2), .B_2(c9_1), .B_1(c9_0), .B_0(BINARY_IN[22]), .O_3(c10_3), .O_2(c10_2), .O_1(c10_1),
    .O_0(c10_0));
  DABLE dable_14 (.B_3(c9_6), .B_2(c9_5), .B_1(c9_4), .B_0(c9_3), .O_3(c10_7), .O_2(c10_6), .O_1(c10_5), .O_0(c10_4));
  DABLE dable_15 (
    .B_3(c9_10), .B_2(c9_9), .B_1(c9_8), .B_0(c9_7), .O_3(c10_11), .O_2(c10_10), .O_1(c10_9), .O_0(c10_8));
  DABLE dable_16 (
    .B_3(c10_2), .B_2(c10_1), .B_1(c10_0), .B_0(BINARY_IN[21]), .O_3(c11_3), .O_2(c11_2), .O_1(c11_1),
    .O_0(c11_0));
  DABLE dable_17 (
    .B_3(c10_6), .B_2(c10_5), .B_1(c10_4), .B_0(c10_3), .O_3(c11_7), .O_2(c11_6), .O_1(c11_5), .O_0(c11_4));
  DABLE dable_18 (
    .B_3(c10_10), .B_2(c10_9), .B_1(c10_8), .B_0(c10_7), .O_3(c11_11), .O_2(c11_10), .O_1(c11_9), .O_0(c11_8));
  DABLE dable_19 (
    .B_3(c11_2), .B_2(c11_1), .B_1(c11_0), .B_0(BINARY_IN[20]), .O_3(c12_3), .O_2(c12_2), .O_1(c12_1),
    .O_0(c12_0));
  DABLE dable_20 (
    .B_3(c11_6), .B_2(c11_5), .B_1(c11_4), .B_0(c11_3), .O_3(c12_7), .O_2(c12_6), .O_1(c12_5), .O_0(c12_4));
  DABLE dable_21 (
    .B_3(c11_10), .B_2(c11_9), .B_1(c11_8), .B_0(c11_7), .O_3(c12_11), .O_2(c12_10), .O_1(c12_9), .O_0(c12_8));
  DABLE dable_22 (
    .B_3(c12_2), .B_2(c12_1), .B_1(c12_0), .B_0(BINARY_IN[19]), .O_3(c13_3), .O_2(c13_2), .O_1(c13_1),
    .O_0(c13_0));
  DABLE dable_23 (
    .B_3(c12_6), .B_2(c12_5), .B_1(c12_4), .B_0(c12_3), .O_3(c13_7), .O_2(c13_6), .O_1(c13_5), .O_0(c13_4));
  DABLE dable_24 (
    .B_3(c12_10), .B_2(c12_9), .B_1(c12_8), .B_0(c12_7), .O_3(c13_11), .O_2(c13_10), .O_1(c13_9), .O_0(c13_8));
  DABLE dable_25 (
    .B_3(c9_11), .B_2(c10_11), .B_1(c11_11), .B_0(c12_11), .O_3(c13_15), .O_2(c13_14), .O_1(c13_13),
    .O_0(c13_12));
  DABLE dable_26 (
    .B_3(c13_2), .B_2(c13_1), .B_1(c13_0), .B_0(BINARY_IN[18]), .O_3(c14_3), .O_2(c14_2), .O_1(c14_1),
    .O_0(c14_0));
  DABLE dable_27 (
    .B_3(c13_6), .B_2(c13_5), .B_1(c13_4), .B_0(c13_3), .O_3(c14_7), .O_2(c14_6), .O_1(c14_5), .O_0(c14_4));
  DABLE dable_28 (
    .B_3(c13_10), .B_2(c13_9), .B_1(c13_8), .B_0(c13_7), .O_3(c14_11), .O_2(c14_10), .O_1(c14_9), .O_0(c14_8));
  DABLE dable_29 (
    .B_3(c13_14), .B_2(c13_13), .B_1(c13_12), .B_0(c13_11), .O_3(c14_15), .O_2(c14_14), .O_1(c14_13),
    .O_0(c14_12));
  DABLE dable_30 (
    .B_3(c14_2), .B_2(c14_1), .B_1(c14_0), .B_0(BINARY_IN[17]), .O_3(c15_3), .O_2(c15_2), .O_1(c15_1),
    .O_0(c15_0));
  DABLE dable_31 (
    .B_3(c14_6), .B_2(c14_5), .B_1(c14_4), .B_0(c14_3), .O_3(c15_7), .O_2(c15_6), .O_1(c15_5), .O_0(c15_4));
  DABLE dable_32 (
    .B_3(c14_10), .B_2(c14_9), .B_1(c14_8), .B_0(c14_7), .O_3(c15_11), .O_2(c15_10), .O_1(c15_9), .O_0(c15_8));
  DABLE dable_33 (
    .B_3(c14_14), .B_2(c14_13), .B_1(c14_12), .B_0(c14_11), .O_3(c15_15), .O_2(c15_14), .O_1(c15_13),
    .O_0(c15_12));
  DABLE dable_34 (
    .B_3(c15_2), .B_2(c15_1), .B_1(c15_0), .B_0(BINARY_IN[16]), .O_3(c16_3), .O_2(c16_2), .O_1(c16_1),
    .O_0(c16_0));
  DABLE dable_35 (
    .B_3(c15_6), .B_2(c15_5), .B_1(c15_4), .B_0(c15_3), .O_3(c16_7), .O_2(c16_6), .O_1(c16_5), .O_0(c16_4));
  DABLE dable_36 (
    .B_3(c15_10), .B_2(c15_9), .B_1(c15_8), .B_0(c15_7), .O_3(c16_11), .O_2(c16_10), .O_1(c16_9), .O_0(c16_8));
  DABLE dable_37 (
    .B_3(c15_14), .B_2(c15_13), .B_1(c15_12), .B_0(c15_11), .O_3(c16_15), .O_2(c16_14), .O_1(c16_13),
    .O_0(c16_12));
  DABLE dable_38 (
    .B_3(1'b0), .B_2(c13_15), .B_1(c14_15), .B_0(c15_15), .O_3(c16_19), .O_2(c16_18), .O_1(c16_17),
    .O_0(c16_16));
  DABLE dable_39 (
    .B_3(c16_2), .B_2(c16_1), .B_1(c16_0), .B_0(BINARY_IN[15]), .O_3(c17_3), .O_2(c17_2), .O_1(c17_1),
    .O_0(c17_0));
  DABLE dable_40 (
    .B_3(c16_6), .B_2(c16_5), .B_1(c16_4), .B_0(c16_3), .O_3(c17_7), .O_2(c17_6), .O_1(c17_5), .O_0(c17_4));
  DABLE dable_41 (
    .B_3(c16_10), .B_2(c16_9), .B_1(c16_8), .B_0(c16_7), .O_3(c17_11), .O_2(c17_10), .O_1(c17_9), .O_0(c17_8));
  DABLE dable_42 (
    .B_3(c16_14), .B_2(c16_13), .B_1(c16_12), .B_0(c16_11), .O_3(c17_15), .O_2(c17_14), .O_1(c17_13),
    .O_0(c17_12));
  DABLE dable_43 (
    .B_3(c16_18), .B_2(c16_17), .B_1(c16_16), .B_0(c16_15), .O_3(c17_19), .O_2(c17_18), .O_1(c17_17),
    .O_0(c17_16));
  DABLE dable_44 (
    .B_3(c17_2), .B_2(c17_1), .B_1(c17_0), .B_0(BINARY_IN[14]), .O_3(c18_3), .O_2(c18_2), .O_1(c18_1),
    .O_0(c18_0));
  DABLE dable_45 (
    .B_3(c17_6), .B_2(c17_5), .B_1(c17_4), .B_0(c17_3), .O_3(c18_7), .O_2(c18_6), .O_1(c18_5), .O_0(c18_4));
  DABLE dable_46 (
    .B_3(c17_10), .B_2(c17_9), .B_1(c17_8), .B_0(c17_7), .O_3(c18_11), .O_2(c18_10), .O_1(c18_9), .O_0(c18_8));
  DABLE dable_47 (
    .B_3(c17_14), .B_2(c17_13), .B_1(c17_12), .B_0(c17_11), .O_3(c18_15), .O_2(c18_14), .O_1(c18_13),
    .O_0(c18_12));
  DABLE dable_48 (
    .B_3(c17_18), .B_2(c17_17), .B_1(c17_16), .B_0(c17_15), .O_3(c18_19), .O_2(c18_18), .O_1(c18_17),
    .O_0(c18_16));
  DABLE dable_49 (
    .B_3(c18_2), .B_2(c18_1), .B_1(c18_0), .B_0(BINARY_IN[13]), .O_3(c19_3), .O_2(c19_2), .O_1(c19_1),
    .O_0(c19_0));
  DABLE dable_50 (
    .B_3(c18_6), .B_2(c18_5), .B_1(c18_4), .B_0(c18_3), .O_3(c19_7), .O_2(c19_6), .O_1(c19_5), .O_0(c19_4));
  DABLE dable_51 (
    .B_3(c18_10), .B_2(c18_9), .B_1(c18_8), .B_0(c18_7), .O_3(c19_11), .O_2(c19_10), .O_1(c19_9), .O_0(c19_8));
  DABLE dable_52 (
    .B_3(c18_14), .B_2(c18_13), .B_1(c18_12), .B_0(c18_11), .O_3(c19_15), .O_2(c19_14), .O_1(c19_13),
    .O_0(c19_12));
  DABLE dable_53 (
    .B_3(c18_18), .B_2(c18_17), .B_1(c18_16), .B_0(c18_15), .O_3(c19_19), .O_2(c19_18), .O_1(c19_17),
    .O_0(c19_16));
  DABLE dable_54 (
    .B_3(1'b0), .B_2(c16_19), .B_1(c17_19), .B_0(c18_19), .O_3(c19_23), .O_2(c19_22), .O_1(c19_21),
    .O_0(c19_20));
  DABLE dable_55 (
    .B_3(c19_2), .B_2(c19_1), .B_1(c19_0), .B_0(BINARY_IN[12]), .O_3(c20_3), .O_2(c20_2), .O_1(c20_1),
    .O_0(c20_0));
  DABLE dable_56 (
    .B_3(c19_6), .B_2(c19_5), .B_1(c19_4), .B_0(c19_3), .O_3(c20_7), .O_2(c20_6), .O_1(c20_5), .O_0(c20_4));
  DABLE dable_57 (
    .B_3(c19_10), .B_2(c19_9), .B_1(c19_8), .B_0(c19_7), .O_3(c20_11), .O_2(c20_10), .O_1(c20_9), .O_0(c20_8));
  DABLE dable_58 (
    .B_3(c19_14), .B_2(c19_13), .B_1(c19_12), .B_0(c19_11), .O_3(c20_15), .O_2(c20_14), .O_1(c20_13),
    .O_0(c20_12));
  DABLE dable_59 (
    .B_3(c19_18), .B_2(c19_17), .B_1(c19_16), .B_0(c19_15), .O_3(c20_19), .O_2(c20_18), .O_1(c20_17),
    .O_0(c20_16));
  DABLE dable_60 (
    .B_3(c19_22), .B_2(c19_21), .B_1(c19_20), .B_0(c19_19), .O_3(c20_23), .O_2(c20_22), .O_1(c20_21),
    .O_0(c20_20));
  DABLE dable_61 (
    .B_3(c20_2), .B_2(c20_1), .B_1(c20_0), .B_0(BINARY_IN[11]), .O_3(c21_3), .O_2(c21_2), .O_1(c21_1),
    .O_0(c21_0));
  DABLE dable_62 (
    .B_3(c20_6), .B_2(c20_5), .B_1(c20_4), .B_0(c20_3), .O_3(c21_7), .O_2(c21_6), .O_1(c21_5), .O_0(c21_4));
  DABLE dable_63 (
    .B_3(c20_10), .B_2(c20_9), .B_1(c20_8), .B_0(c20_7), .O_3(c21_11), .O_2(c21_10), .O_1(c21_9), .O_0(c21_8));
  DABLE dable_64 (
    .B_3(c20_14), .B_2(c20_13), .B_1(c20_12), .B_0(c20_11), .O_3(c21_15), .O_2(c21_14), .O_1(c21_13),
    .O_0(c21_12));
  DABLE dable_65 (
    .B_3(c20_18), .B_2(c20_17), .B_1(c20_16), .B_0(c20_15), .O_3(c21_19), .O_2(c21_18), .O_1(c21_17),
    .O_0(c21_16));
  DABLE dable_66 (
    .B_3(c20_22), .B_2(c20_21), .B_1(c20_20), .B_0(c20_19), .O_3(c21_23), .O_2(c21_22), .O_1(c21_21),
    .O_0(c21_20));
  DABLE dable_67 (
    .B_3(c21_2), .B_2(c21_1), .B_1(c21_0), .B_0(BINARY_IN[10]), .O_3(c22_3), .O_2(c22_2), .O_1(c22_1),
    .O_0(c22_0));
  DABLE dable_68 (
    .B_3(c21_6), .B_2(c21_5), .B_1(c21_4), .B_0(c21_3), .O_3(c22_7), .O_2(c22_6), .O_1(c22_5), .O_0(c22_4));
  DABLE dable_69 (
    .B_3(c21_10), .B_2(c21_9), .B_1(c21_8), .B_0(c21_7), .O_3(c22_11), .O_2(c22_10), .O_1(c22_9), .O_0(c22_8));
  DABLE dable_70 (
    .B_3(c21_14), .B_2(c21_13), .B_1(c21_12), .B_0(c21_11), .O_3(c22_15), .O_2(c22_14), .O_1(c22_13),
    .O_0(c22_12));
  DABLE dable_71 (
    .B_3(c21_18), .B_2(c21_17), .B_1(c21_16), .B_0(c21_15), .O_3(c22_19), .O_2(c22_18), .O_1(c22_17),
    .O_0(c22_16));
  DABLE dable_72 (
    .B_3(c21_22), .B_2(c21_21), .B_1(c21_20), .B_0(c21_19), .O_3(c22_23), .O_2(c22_22), .O_1(c22_21),
    .O_0(c22_20));
  DABLE dable_73 (
    .B_3(c22_2), .B_2(c22_1), .B_1(c22_0), .B_0(BINARY_IN[9]), .O_3(c23_3), .O_2(c23_2), .O_1(c23_1),
    .O_0(c23_0));
  DABLE dable_74 (
    .B_3(c22_6), .B_2(c22_5), .B_1(c22_4), .B_0(c22_3), .O_3(c23_7), .O_2(c23_6), .O_1(c23_5), .O_0(c23_4));
  DABLE dable_75 (
    .B_3(c22_10), .B_2(c22_9), .B_1(c22_8), .B_0(c22_7), .O_3(c23_11), .O_2(c23_10), .O_1(c23_9), .O_0(c23_8));
  DABLE dable_76 (
    .B_3(c22_14), .B_2(c22_13), .B_1(c22_12), .B_0(c22_11), .O_3(c23_15), .O_2(c23_14), .O_1(c23_13),
    .O_0(c23_12));
  DABLE dable_77 (
    .B_3(c22_18), .B_2(c22_17), .B_1(c22_16), .B_0(c22_15), .O_3(c23_19), .O_2(c23_18), .O_1(c23_17),
    .O_0(c23_16));
  DABLE dable_78 (
    .B_3(c22_22), .B_2(c22_21), .B_1(c22_20), .B_0(c22_19), .O_3(c23_23), .O_2(c23_22), .O_1(c23_21),
    .O_0(c23_20));
  DABLE dable_79 (
    .B_3(c19_23), .B_2(c20_23), .B_1(c21_23), .B_0(c22_23), .O_3(c23_27), .O_2(c23_26), .O_1(c23_25),
    .O_0(c23_24));
  DABLE dable_80 (
    .B_3(c23_2), .B_2(c23_1), .B_1(c23_0), .B_0(BINARY_IN[8]), .O_3(c24_3), .O_2(c24_2), .O_1(c24_1),
    .O_0(c24_0));
  DABLE dable_81 (
    .B_3(c23_6), .B_2(c23_5), .B_1(c23_4), .B_0(c23_3), .O_3(c24_7), .O_2(c24_6), .O_1(c24_5), .O_0(c24_4));
  DABLE dable_82 (
    .B_3(c23_10), .B_2(c23_9), .B_1(c23_8), .B_0(c23_7), .O_3(c24_11), .O_2(c24_10), .O_1(c24_9), .O_0(c24_8));
  DABLE dable_83 (
    .B_3(c23_14), .B_2(c23_13), .B_1(c23_12), .B_0(c23_11), .O_3(c24_15), .O_2(c24_14), .O_1(c24_13),
    .O_0(c24_12));
  DABLE dable_84 (
    .B_3(c23_18), .B_2(c23_17), .B_1(c23_16), .B_0(c23_15), .O_3(c24_19), .O_2(c24_18), .O_1(c24_17),
    .O_0(c24_16));
  DABLE dable_85 (
    .B_3(c23_22), .B_2(c23_21), .B_1(c23_20), .B_0(c23_19), .O_3(c24_23), .O_2(c24_22), .O_1(c24_21),
    .O_0(c24_20));
  DABLE dable_86 (
    .B_3(c23_26), .B_2(c23_25), .B_1(c23_24), .B_0(c23_23), .O_3(c24_27), .O_2(c24_26), .O_1(c24_25),
    .O_0(c24_24));
  DABLE dable_87 (
    .B_3(c24_2), .B_2(c24_1), .B_1(c24_0), .B_0(BINARY_IN[7]), .O_3(c25_3), .O_2(c25_2), .O_1(c25_1),
    .O_0(c25_0));
  DABLE dable_88 (
    .B_3(c24_6), .B_2(c24_5), .B_1(c24_4), .B_0(c24_3), .O_3(c25_7), .O_2(c25_6), .O_1(c25_5), .O_0(c25_4));
  DABLE dable_89 (
    .B_3(c24_10), .B_2(c24_9), .B_1(c24_8), .B_0(c24_7), .O_3(c25_11), .O_2(c25_10), .O_1(c25_9), .O_0(c25_8));
  DABLE dable_90 (
    .B_3(c24_14), .B_2(c24_13), .B_1(c24_12), .B_0(c24_11), .O_3(c25_15), .O_2(c25_14), .O_1(c25_13),
    .O_0(c25_12));
  DABLE dable_91 (
    .B_3(c24_18), .B_2(c24_17), .B_1(c24_16), .B_0(c24_15), .O_3(c25_19), .O_2(c25_18), .O_1(c25_17),
    .O_0(c25_16));
  DABLE dable_92 (
    .B_3(c24_22), .B_2(c24_21), .B_1(c24_20), .B_0(c24_19), .O_3(c25_23), .O_2(c25_22), .O_1(c25_21),
    .O_0(c25_20));
  DABLE dable_93 (
    .B_3(c24_26), .B_2(c24_25), .B_1(c24_24), .B_0(c24_23), .O_3(c25_27), .O_2(c25_26), .O_1(c25_25),
    .O_0(c25_24));
  DABLE dable_94 (
    .B_3(c25_2), .B_2(c25_1), .B_1(c25_0), .B_0(BINARY_IN[6]), .O_3(c26_3), .O_2(c26_2), .O_1(c26_1),
    .O_0(c26_0));
  DABLE dable_95 (
    .B_3(c25_6), .B_2(c25_5), .B_1(c25_4), .B_0(c25_3), .O_3(c26_7), .O_2(c26_6), .O_1(c26_5), .O_0(c26_4));
  DABLE dable_96 (
    .B_3(c25_10), .B_2(c25_9), .B_1(c25_8), .B_0(c25_7), .O_3(c26_11), .O_2(c26_10), .O_1(c26_9), .O_0(c26_8));
  DABLE dable_97 (
    .B_3(c25_14), .B_2(c25_13), .B_1(c25_12), .B_0(c25_11), .O_3(c26_15), .O_2(c26_14), .O_1(c26_13),
    .O_0(c26_12));
  DABLE dable_98 (
    .B_3(c25_18), .B_2(c25_17), .B_1(c25_16), .B_0(c25_15), .O_3(c26_19), .O_2(c26_18), .O_1(c26_17),
    .O_0(c26_16));
  DABLE dable_99 (
    .B_3(c25_22), .B_2(c25_21), .B_1(c25_20), .B_0(c25_19), .O_3(c26_23), .O_2(c26_22), .O_1(c26_21),
    .O_0(c26_20));
  DABLE dable_100 (
    .B_3(c25_26), .B_2(c25_25), .B_1(c25_24), .B_0(c25_23), .O_3(c26_27), .O_2(c26_26), .O_1(c26_25),
    .O_0(c26_24));
  DABLE dable_101 (
    .B_3(1'b0), .B_2(c23_27), .B_1(c24_27), .B_0(c25_27), .O_2(c26_30), .O_1(c26_29), .O_0(c26_28));  // open: O_3
  DABLE dable_102 (
    .B_3(c26_2), .B_2(c26_1), .B_1(c26_0), .B_0(BINARY_IN[5]), .O_3(c27_3), .O_2(c27_2), .O_1(c27_1),
    .O_0(c27_0));
  DABLE dable_103 (
    .B_3(c26_6), .B_2(c26_5), .B_1(c26_4), .B_0(c26_3), .O_3(c27_7), .O_2(c27_6), .O_1(c27_5), .O_0(c27_4));
  DABLE dable_104 (
    .B_3(c26_10), .B_2(c26_9), .B_1(c26_8), .B_0(c26_7), .O_3(c27_11), .O_2(c27_10), .O_1(c27_9), .O_0(c27_8));
  DABLE dable_105 (
    .B_3(c26_14), .B_2(c26_13), .B_1(c26_12), .B_0(c26_11), .O_3(c27_15), .O_2(c27_14), .O_1(c27_13),
    .O_0(c27_12));
  DABLE dable_106 (
    .B_3(c26_18), .B_2(c26_17), .B_1(c26_16), .B_0(c26_15), .O_3(c27_19), .O_2(c27_18), .O_1(c27_17),
    .O_0(c27_16));
  DABLE dable_107 (
    .B_3(c26_22), .B_2(c26_21), .B_1(c26_20), .B_0(c26_19), .O_3(c27_23), .O_2(c27_22), .O_1(c27_21),
    .O_0(c27_20));
  DABLE dable_108 (
    .B_3(c26_26), .B_2(c26_25), .B_1(c26_24), .B_0(c26_23), .O_3(c27_27), .O_2(c27_26), .O_1(c27_25),
    .O_0(c27_24));
  DABLE dable_109 (
    .B_3(c26_30), .B_2(c26_29), .B_1(c26_28), .B_0(c26_27), .O_2(c27_30), .O_1(c27_29), .O_0(c27_28));  // open: O_3
  DABLE dable_110 (
    .B_3(c27_2), .B_2(c27_1), .B_1(c27_0), .B_0(BINARY_IN[4]), .O_3(c28_3), .O_2(c28_2), .O_1(c28_1),
    .O_0(c28_0));
  DABLE dable_111 (
    .B_3(c27_6), .B_2(c27_5), .B_1(c27_4), .B_0(c27_3), .O_3(c28_7), .O_2(c28_6), .O_1(c28_5), .O_0(c28_4));
  DABLE dable_112 (
    .B_3(c27_10), .B_2(c27_9), .B_1(c27_8), .B_0(c27_7), .O_3(c28_11), .O_2(c28_10), .O_1(c28_9), .O_0(c28_8));
  DABLE dable_113 (
    .B_3(c27_14), .B_2(c27_13), .B_1(c27_12), .B_0(c27_11), .O_3(c28_15), .O_2(c28_14), .O_1(c28_13),
    .O_0(c28_12));
  DABLE dable_114 (
    .B_3(c27_18), .B_2(c27_17), .B_1(c27_16), .B_0(c27_15), .O_3(c28_19), .O_2(c28_18), .O_1(c28_17),
    .O_0(c28_16));
  DABLE dable_115 (
    .B_3(c27_22), .B_2(c27_21), .B_1(c27_20), .B_0(c27_19), .O_3(c28_23), .O_2(c28_22), .O_1(c28_21),
    .O_0(c28_20));
  DABLE dable_116 (
    .B_3(c27_26), .B_2(c27_25), .B_1(c27_24), .B_0(c27_23), .O_3(c28_27), .O_2(c28_26), .O_1(c28_25),
    .O_0(c28_24));
  DABLE dable_117 (
    .B_3(c27_30), .B_2(c27_29), .B_1(c27_28), .B_0(c27_27), .O_2(c28_30), .O_1(c28_29), .O_0(c28_28));  // open: O_3
  DABLE dable_118 (
    .B_3(c28_2), .B_2(c28_1), .B_1(c28_0), .B_0(BINARY_IN[3]), .O_3(c29_3), .O_2(c29_2), .O_1(c29_1),
    .O_0(c29_0));
  DABLE dable_119 (
    .B_3(c28_6), .B_2(c28_5), .B_1(c28_4), .B_0(c28_3), .O_3(c29_7), .O_2(c29_6), .O_1(c29_5), .O_0(c29_4));
  DABLE dable_120 (
    .B_3(c28_10), .B_2(c28_9), .B_1(c28_8), .B_0(c28_7), .O_3(c29_11), .O_2(c29_10), .O_1(c29_9), .O_0(c29_8));
  DABLE dable_121 (
    .B_3(c28_14), .B_2(c28_13), .B_1(c28_12), .B_0(c28_11), .O_3(c29_15), .O_2(c29_14), .O_1(c29_13),
    .O_0(c29_12));
  DABLE dable_122 (
    .B_3(c28_18), .B_2(c28_17), .B_1(c28_16), .B_0(c28_15), .O_3(c29_19), .O_2(c29_18), .O_1(c29_17),
    .O_0(c29_16));
  DABLE dable_123 (
    .B_3(c28_22), .B_2(c28_21), .B_1(c28_20), .B_0(c28_19), .O_3(c29_23), .O_2(c29_22), .O_1(c29_21),
    .O_0(c29_20));
  DABLE dable_124 (
    .B_3(c28_26), .B_2(c28_25), .B_1(c28_24), .B_0(c28_23), .O_3(c29_27), .O_2(c29_26), .O_1(c29_25),
    .O_0(c29_24));
  DABLE dable_125 (
    .B_3(c28_30), .B_2(c28_29), .B_1(c28_28), .B_0(c28_27), .O_2(c29_30), .O_1(c29_29), .O_0(c29_28));  // open: O_3
  DABLE dable_126 (
    .B_3(c29_2), .B_2(c29_1), .B_1(c29_0), .B_0(BINARY_IN[2]), .O_3(c30_3), .O_2(c30_2), .O_1(c30_1),
    .O_0(c30_0));
  DABLE dable_127 (
    .B_3(c29_6), .B_2(c29_5), .B_1(c29_4), .B_0(c29_3), .O_3(c30_7), .O_2(c30_6), .O_1(c30_5), .O_0(c30_4));
  DABLE dable_128 (
    .B_3(c29_10), .B_2(c29_9), .B_1(c29_8), .B_0(c29_7), .O_3(c30_11), .O_2(c30_10), .O_1(c30_9), .O_0(c30_8));
  DABLE dable_129 (
    .B_3(c29_14), .B_2(c29_13), .B_1(c29_12), .B_0(c29_11), .O_3(c30_15), .O_2(c30_14), .O_1(c30_13),
    .O_0(c30_12));
  DABLE dable_130 (
    .B_3(c29_18), .B_2(c29_17), .B_1(c29_16), .B_0(c29_15), .O_3(c30_19), .O_2(c30_18), .O_1(c30_17),
    .O_0(c30_16));
  DABLE dable_131 (
    .B_3(c29_22), .B_2(c29_21), .B_1(c29_20), .B_0(c29_19), .O_3(c30_23), .O_2(c30_22), .O_1(c30_21),
    .O_0(c30_20));
  DABLE dable_132 (
    .B_3(c29_26), .B_2(c29_25), .B_1(c29_24), .B_0(c29_23), .O_3(c30_27), .O_2(c30_26), .O_1(c30_25),
    .O_0(c30_24));
  DABLE dable_133 (
    .B_3(c29_30), .B_2(c29_29), .B_1(c29_28), .B_0(c29_27), .O_2(c30_30), .O_1(c30_29), .O_0(c30_28));  // open: O_3
  DABLE dable_134 (
    .B_3(c30_2), .B_2(c30_1), .B_1(c30_0), .B_0(BINARY_IN[1]), .O_3(DIGIT_1[0]), .O_2(DIGIT_0[3]),
    .O_1(DIGIT_0[2]), .O_0(DIGIT_0[1]));
  DABLE dable_135 (
    .B_3(c30_6), .B_2(c30_5), .B_1(c30_4), .B_0(c30_3), .O_3(DIGIT_2[0]), .O_2(DIGIT_1[3]), .O_1(DIGIT_1[2]),
    .O_0(DIGIT_1[1]));
  DABLE dable_136 (
    .B_3(c30_10), .B_2(c30_9), .B_1(c30_8), .B_0(c30_7), .O_3(DIGIT_3[0]), .O_2(DIGIT_2[3]),
    .O_1(DIGIT_2[2]), .O_0(DIGIT_2[1]));
  DABLE dable_137 (
    .B_3(c30_14), .B_2(c30_13), .B_1(c30_12), .B_0(c30_11), .O_3(DIGIT_4[0]), .O_2(DIGIT_3[3]),
    .O_1(DIGIT_3[2]), .O_0(DIGIT_3[1]));
  DABLE dable_138 (
    .B_3(c30_18), .B_2(c30_17), .B_1(c30_16), .B_0(c30_15), .O_3(DIGIT_5[0]), .O_2(DIGIT_4[3]),
    .O_1(DIGIT_4[2]), .O_0(DIGIT_4[1]));
  DABLE dable_139 (
    .B_3(c30_22), .B_2(c30_21), .B_1(c30_20), .B_0(c30_19), .O_3(DIGIT_6[0]), .O_2(DIGIT_5[3]),
    .O_1(DIGIT_5[2]), .O_0(DIGIT_5[1]));
  DABLE dable_140 (
    .B_3(c30_26), .B_2(c30_25), .B_1(c30_24), .B_0(c30_23), .O_3(DIGIT_7[0]), .O_2(DIGIT_6[3]),
    .O_1(DIGIT_6[2]), .O_0(DIGIT_6[1]));
  DABLE dable_141 (
    .B_3(c30_30), .B_2(c30_29), .B_1(c30_28), .B_0(c30_27), .O_2(DIGIT_7[3]), .O_1(DIGIT_7[2]),
    .O_0(DIGIT_7[1]));  // open: O_3

  assign DIGIT_0[0] = BINARY_IN[0];

  // Other names for the same wires on the sheet: in1 = BINARY_IN[1]; in2 = BINARY_IN[2]; in3 = BINARY_IN[3];
  //   in4 = BINARY_IN[4]; in5 = BINARY_IN[5]; in6 = BINARY_IN[6]; in7 = BINARY_IN[7]; in8 = BINARY_IN[8];
  //   in9 = BINARY_IN[9]; in10 = BINARY_IN[10]; in11 = BINARY_IN[11]; in12 = BINARY_IN[12]; in13 = BINARY_IN[13];
  //   in14 = BINARY_IN[14]; in15 = BINARY_IN[15]; in16 = BINARY_IN[16]; in17 = BINARY_IN[17]; in18 = BINARY_IN[18];
  //   in19 = BINARY_IN[19]; in20 = BINARY_IN[20]; in21 = BINARY_IN[21]; in22 = BINARY_IN[22]; in23 = BINARY_IN[23];
  //   in24 = BINARY_IN[24]; in25 = BINARY_IN[25]; in26 = BINARY_IN[26]; in27 = BINARY_IN[27]; in28 = BINARY_IN[28];
  //   in29 = BINARY_IN[29]; in30 = BINARY_IN[30]; in31 = BINARY_IN[31]; in0 = BINARY_IN[0]; c31_0 = DIGIT_0[1];
  //   c31_1 = DIGIT_0[2]; c31_2 = DIGIT_0[3]; c31_3 = DIGIT_1[0]; c31_4 = DIGIT_1[1]; c31_5 = DIGIT_1[2];
  //   c31_6 = DIGIT_1[3]; c31_7 = DIGIT_2[0]; c31_8 = DIGIT_2[1]; c31_9 = DIGIT_2[2]; c31_10 = DIGIT_2[3];
  //   c31_11 = DIGIT_3[0]; c31_12 = DIGIT_3[1]; c31_13 = DIGIT_3[2]; c31_14 = DIGIT_3[3]; c31_15 = DIGIT_4[0];
  //   c31_16 = DIGIT_4[1]; c31_17 = DIGIT_4[2]; c31_18 = DIGIT_4[3]; c31_19 = DIGIT_5[0]; c31_20 = DIGIT_5[1];
  //   c31_21 = DIGIT_5[2]; c31_22 = DIGIT_5[3]; c31_23 = DIGIT_6[0]; c31_24 = DIGIT_6[1]; c31_25 = DIGIT_6[2];
  //   c31_26 = DIGIT_6[3]; c31_27 = DIGIT_7[0]; c31_28 = DIGIT_7[1]; c31_29 = DIGIT_7[2]; c31_30 = DIGIT_7[3]
endmodule

module CALCULATOR (
);

  wire button_1_out, button_2_out, button_3_out, button_4_out, button_5_out, button_6_out, button_7_out,
       button_8_out, button_9_out, button_10_out, button_11_out, button_12_out, button_13_out, button_14_out,
       button_15_out, button_16_out;
  wire [3:0] calculator_body_1_d_0, calculator_body_1_d_1, calculator_body_1_d_2, calculator_body_1_d_3,
       calculator_body_1_d_4, calculator_body_1_d_5, calculator_body_1_d_6, calculator_body_1_d_7;

  Hex_Digit_Display hex_digit_display_1 (.value(calculator_body_1_d_7));  // open: dp
  Hex_Digit_Display hex_digit_display_2 (.value(calculator_body_1_d_6));  // open: dp
  Hex_Digit_Display hex_digit_display_3 (.value(calculator_body_1_d_5));  // open: dp
  calculator_body calculator_body_1 (
    .N_9(button_1_out), .N_8(button_2_out), .N_7(button_3_out), .N_6(button_4_out), .N_5(button_5_out),
    .N_4(button_8_out), .N_3(button_9_out), .N_2(button_6_out), .N_1(button_7_out), .N_0(button_10_out),
    .ADD(button_11_out), .SUB(button_12_out), .MUL(button_13_out), .DIV(button_14_out),
    .equal(button_15_out), .clear(button_16_out), .D_7(calculator_body_1_d_7), .D_6(calculator_body_1_d_6),
    .D_5(calculator_body_1_d_5), .D_4(calculator_body_1_d_4), .D_3(calculator_body_1_d_3),
    .D_2(calculator_body_1_d_2), .D_1(calculator_body_1_d_1), .D_0(calculator_body_1_d_0));
  Button button_1 (.out(button_1_out));
  Hex_Digit_Display hex_digit_display_4 (.value(calculator_body_1_d_4));  // open: dp
  Hex_Digit_Display hex_digit_display_5 (.value(calculator_body_1_d_3));  // open: dp
  Button button_2 (.out(button_2_out));
  Button button_3 (.out(button_3_out));
  Button button_4 (.out(button_4_out));
  Button button_5 (.out(button_5_out));
  Hex_Digit_Display hex_digit_display_6 (.value(calculator_body_1_d_1));  // open: dp
  Hex_Digit_Display hex_digit_display_7 (.value(calculator_body_1_d_2));  // open: dp
  Button button_6 (.out(button_6_out));
  Button button_7 (.out(button_7_out));
  Button button_8 (.out(button_8_out));
  Button button_9 (.out(button_9_out));
  Hex_Digit_Display hex_digit_display_8 (.value(calculator_body_1_d_0));  // open: dp
  Button button_10 (.out(button_10_out));
  Button button_11 (.out(button_11_out));
  Button button_12 (.out(button_12_out));
  Button button_13 (.out(button_13_out));
  Button button_14 (.out(button_14_out));
  Button button_15 (.out(button_15_out));
  Button button_16 (.out(button_16_out));
endmodule
